# Fritzing sketch astable-transistor-circuit (saved by Fritzing 0.8.7b)
breadboards: 1

parts:
  LT = NPN-Transistor [part_number=2N3904 package="TO92 [THT]"]
  RT = NPN-Transistor [part_number=2N3904 package="TO92 [THT]"]
  C1 = Electrolytic Capacitor [capacitance=1µF package="100 mil [THT, electrolytic]"]
  C2 = Electrolytic Capacitor [capacitance=1µF package="100 mil [THT, electrolytic]"]
  R1 = Resistor [tolerance=±5% resistance=1k package=THT]
  R2 = Resistor [tolerance=±5% resistance=100k package=THT]
  R3 = Resistor [tolerance=±5% resistance=100k package=THT]
  R4 = Resistor [tolerance=±5% resistance=1k package=THT]
  POWER = DC Power [voltage=5V]

nets:
  GND: LT.E, RT.E, POWER.V-
  N1: LT.B, C1.-, R2.Pin_0
  N2: LT.C, C2.+, R4.Pin_0
  N3: RT.B, C2.-, R3.Pin_0
  N4: RT.C, C1.+, R1.Pin_0
  N5: R1.Pin_1, R2.Pin_1, R3.Pin_1, R4.Pin_1, POWER.V+
