# Fritzing sketch tmp36-breadboard-circuit (saved by Fritzing 0.7.7b)
breadboards: 1

parts:
  Part1 = Arduino Pro Mini 3.3V
  T1 = TMP36 Temperature Sensor [package="TO92 [THT]"]
  Part2 = OpenLog
  VCC1 = Battery

nets:
  VCC: Part1.VCC, T1.+Vs, Part2.VCC, VCC1.+
  N1: Part1.A0, T1.Vout
  N2: Part1.TXO, Part2.RXI
  GND: T1.GND, Part2.GND, VCC1.-

notes:
  3.3V TO BREADBOARD
  Check datasheet
  order of pins
