# Fritzing sketch transistor-gate-and (saved by Fritzing 0.8.3b)
breadboards: 1

parts:
  Q1 = NPN-Transistor [package="TO92 [THT]"]
  Q2 = NPN-Transistor [package="TO92 [THT]"]
  Part1 = Arduino Pro Mini v13
  R1 = Resistor [tolerance=±5% resistance=10k package=THT]
  R2 = Resistor [tolerance=±5% resistance=10k package=THT]
  R3 = Resistor [tolerance=±5% resistance=1k package=THT]
  LED1 = LED - 5mm [color="Red (633nm)" package="5 mm [THT]"]
  R4 = Resistor [tolerance=±5% resistance=1k package=THT]

nets:
  N1: Q1.E, Q2.C
  N2: Q1.B, R1.Pin_0
  N3: Q1.C, Part1.VCC
  N4: Q2.E, R3.Pin_0, R4.Pin_1
  N5: Q2.B, R2.Pin_0
  N6: Part1.D9_PWM, R2.Pin_1
  N7: Part1.D8, R1.Pin_1
  N8: Part1.GND, R3.Pin_1, LED1.cathode
  N9: LED1.anode, R4.Pin_0

notes:
  INPUT A
  Pin 8
  INPUT B
  Pin 9
